// Logisim project Serie_1_parcial_3DiegoSolis.circ as structural Verilog
module full_adder (
  input  a,
  input  b,
  input  cin,
  output s,
  output Cout
);

  wire and_1_out, and_2_out, xor_1_out;

  xor xor_1 (xor_1_out, a, b);
  xor xor_2 (s, xor_1_out, cin);
  and and_1 (and_1_out, cin, xor_1_out);
  and and_2 (and_2_out, b, a);
  or or_1 (Cout, and_1_out, and_2_out);
endmodule

module Ripple (
  input  a0,
  input  b0,
  input  cin,
  input  a1,
  input  b1,
  input  a2,
  input  b2,
  input  a3,
  input  b3,
  output s0,
  output s1,
  output s2,
  output s3,
  output Cout
);

  wire full_adder_1_cout, full_adder_2_cout, full_adder_3_cout;

  full_adder full_adder_1 (.a(a0), .b(b0), .cin(cin), .s(s0), .Cout(full_adder_1_cout));
  full_adder full_adder_2 (.a(a1), .b(b1), .cin(full_adder_1_cout), .s(s1), .Cout(full_adder_2_cout));
  full_adder full_adder_3 (.a(a2), .b(b2), .cin(full_adder_2_cout), .s(s2), .Cout(full_adder_3_cout));
  full_adder full_adder_4 (.a(a3), .b(b3), .cin(full_adder_3_cout), .s(s3), .Cout(Cout));
endmodule

module carry (
  input  g0,
  input  po,
  input  cin,
  input  g1,
  input  p1,
  input  g2,
  input  p2,
  input  g3,
  input  p3,
  output c0,
  output c1,
  output c2,
  output c3
);

  wire and_1_out, and_3_out, and_4_out, and_5_out, and_6_out, and_7_out, and_8_out, and_9_out, and_10_out;

  and and_1 (and_1_out, g3, cin);
  and and_2 (cin, g0, p1, p2);
  and and_3 (and_3_out, g1, p2);
  and and_4 (and_4_out, g1, p2, p3);
  and and_5 (and_5_out, g2, p3);
  and and_6 (and_6_out, cin, p1, g3);
  and and_7 (and_7_out, g0, p1);
  and and_8 (and_8_out, cin, g3, p1, p2);
  and and_9 (and_9_out, g0, p1, p2, p3);
  or or_1 (c0, g0, and_1_out);
  or or_2 (c1, g1, and_6_out, and_7_out);
  and and_10 (and_10_out, cin, g3, p1, p2, p3);
  or or_3 (c2, g2, cin, and_8_out, and_3_out);
  or or_4 (c3, g3, and_9_out, and_4_out, and_10_out, and_5_out);

  assign po = g3;
endmodule

module adder_2 (
  input  a,
  input  b,
  input  Cin,
  output p,
  output g,
  output s
);

  wire and_1_out, or_1_out;

  xor xor_1 (p, a, b);
  and and_1 (and_1_out, p, Cin);
  and and_2 (g, a, b);
  xor xor_2 (s, p, Cin);
  or or_1 (or_1_out, and_1_out, g);
endmodule

module Carry_lookahead (
  input  a0,
  input  Cin,
  input  b0,
  input  a1,
  input  b1,
  input  a2,
  input  b2,
  input  a3,
  input  b3,
  output s0,
  output s1,
  output s2,
  output s3
);

  wire c0, c1, c2, c3, g0, g1, g2, g3, p0, p1, p2, p3;

  adder_2 adder_2_1 (.a(a0), .b(b0), .Cin(Cin), .p(p0), .g(g0), .s(s0));
  adder_2 adder_2_2 (.a(a1), .b(b1), .Cin(c0), .p(p1), .g(g1), .s(s1));
  adder_2 adder_2_3 (.a(a2), .b(b2), .Cin(c1), .p(p2), .g(g2), .s(s2));
  adder_2 adder_2_4 (.a(a3), .b(b3), .Cin(c2), .p(p3), .g(g3), .s(s3));
  carry carry_1 (
    .g0(g0), .po(p0), .cin(Cin), .g1(g1), .p1(p1), .g2(g2), .p2(p2), .g3(g3), .p3(p3), .c0(c0), .c1(c1),
    .c2(c2), .c3(c3));
endmodule

module p_g (
  input  [3:0] a,
  input  [3:0] b,
  output p0,
  output g0,
  output p1,
  output g1,
  output p2,
  output g2,
  output p3,
  output g3
);

  and and_1 (g0, b[0], a[0]);
  and and_2 (g1, b[1], a[1]);
  and and_3 (g2, b[2], a[2]);
  and and_4 (g3, b[3], a[3]);
  or or_1 (p0, b[0], a[0]);
  or or_2 (p1, b[1], a[1]);
  or or_3 (p2, b[2], a[2]);
  or or_4 (p3, b[3], a[3]);
endmodule

module pre_levels (
  input  [3:0] p,
  input  [3:0] g,
  input  Cin,
  output g0_out,
  output g1_out,
  output g2_out,
  output g3_out,
  output Cout
);

  wire and_1_out, and_2_out, and_3_out, and_4_out, and_5_out, and_6_out, or_3_out;

  and and_1 (and_1_out, Cin, p[0]);
  and and_2 (and_2_out, g1_out, p[1]);
  and and_3 (and_3_out, p[1], p[2]);
  or or_1 (g1_out, g[0], and_1_out);
  or or_2 (g2_out, g[1], and_2_out);
  and and_4 (and_4_out, g[1], p[2]);
  and and_5 (and_5_out, g1_out, and_3_out);
  or or_3 (or_3_out, and_4_out, g[2]);
  or or_4 (g3_out, or_3_out, and_5_out);
  and and_6 (and_6_out, g3_out, p[3]);
  or or_5 (Cout, and_6_out, g[3]);

  assign g0_out = Cin;
endmodule

module pre_adders (
  input  [3:0] a,
  input  [3:0] b,
  input  [3:0] g_out,
  output s0,
  output s1,
  output s2,
  output s3
);

  wire xor_1_out, xor_2_out, xor_3_out, xor_4_out;

  xor xor_1 (xor_1_out, b[0], a[0]);
  xor xor_2 (xor_2_out, b[1], a[1]);
  xor xor_3 (xor_3_out, b[2], a[2]);
  xor xor_4 (xor_4_out, b[3], a[3]);
  xor xor_5 (s0, xor_1_out, g_out[0]);
  xor xor_6 (s1, g_out[1], xor_2_out);
  xor xor_7 (s2, g_out[2], xor_3_out);
  xor xor_8 (s3, g_out[3], xor_4_out);
endmodule

module Prefix_adder (
  input  [3:0] b,
  input  [3:0] a,
  input  Cin,
  output s3,
  output s2,
  output s1,
  output s0,
  output cout
);

  wire [3:0] p_g_1_g0, p_g_1_p0, pre_levels_1_g0_out;

  p_g p_g_1 (
    .a(a), .b(b), .p0(p_g_1_p0[0]), .g0(p_g_1_g0[0]), .p1(p_g_1_p0[1]), .g1(p_g_1_g0[1]), .p2(p_g_1_p0[2]),
    .g2(p_g_1_g0[2]), .p3(p_g_1_p0[3]), .g3(p_g_1_g0[3]));
  pre_levels pre_levels_1 (
    .p(p_g_1_p0), .g(p_g_1_g0), .Cin(Cin), .g0_out(pre_levels_1_g0_out[0]), .g1_out(pre_levels_1_g0_out[1]),
    .g2_out(pre_levels_1_g0_out[2]), .g3_out(pre_levels_1_g0_out[3]), .Cout(cout));
  pre_adders pre_adders_1 (.a(a), .b(b), .g_out(pre_levels_1_g0_out), .s0(s0), .s1(s1), .s2(s2), .s3(s3));
endmodule
