// Logisim project AluvFinalDiegoSolis.circ as structural Verilog
module add (
  input  a,
  input  b,
  input  cin,
  output s,
  output Cout
);

  wire and_1_out, and_2_out, xor_1_out;

  xor xor_1 (xor_1_out, a, b);
  xor xor_2 (s, xor_1_out, cin);
  and and_1 (and_1_out, cin, xor_1_out);
  and and_2 (and_2_out, b, a);
  or or_1 (Cout, and_1_out, and_2_out);
endmodule

module Circ_add (
  input  res,
  input  [5:0] B,
  input  [5:0] A,
  output [5:0] S,
  output Over,
  output cero,
  output negativo,
  output Cout
);

  wire Cou_0, Cou_1, Cou_2, Cou_3, Cou_4, or_1_out;

  xor xor_1 (Over, Cou_4, Cout);
  add add_1 (.a(A[0]), .b(B[0]), .cin(res), .s(S[0]), .Cout(Cou_0));
  add add_2 (.a(A[1]), .b(B[1]), .cin(Cou_0), .s(S[1]), .Cout(Cou_1));
  add add_3 (.a(A[2]), .b(B[2]), .cin(Cou_1), .s(S[2]), .Cout(Cou_2));
  add add_4 (.a(A[3]), .b(B[3]), .cin(Cou_2), .s(S[3]), .Cout(Cou_3));
  add add_5 (.a(A[4]), .b(B[4]), .cin(Cou_3), .s(S[4]), .Cout(Cou_4));
  add add_6 (.a(A[5]), .b(B[5]), .cin(Cou_4), .s(S[5]), .Cout(Cout));
  or or_1 (or_1_out, S[0], S[1], S[2], S[3], S[4], S[5]);
  and and_1 (negativo, S[5], res);
  not not_1 (cero, or_1_out);

  // Other names for the same wires on the sheet: cou = Cout
endmodule

module cir_rest_sum (
  input  AL,
  input  [5:0] B,
  input  [5:0] A,
  output [5:0] SumyRest,
  output Cout,
  output over
);

  wire [5:0] multiplexer_1_out, not_1_out;

  assign not_1_out = ~B;  // NOT_Gate not_1, 6 bits wide
  Multiplexer #(.width(6)) multiplexer_1 (.in0(B), .in1(not_1_out), .out(multiplexer_1_out), .sel(AL));
  Circ_add circ_add_1 (
    .res(AL), .B(multiplexer_1_out), .A(A), .S(SumyRest), .Over(over), .cero(Cout));  // open: negativo, Cout
endmodule

module Cir_and (
  input  [5:0] B,
  input  [5:0] A,
  output [5:0] out_and
);

  assign out_and = B & A;  // AND_Gate and_1, 6 bits wide
endmodule

module Circ_or (
  input  [5:0] B,
  input  [5:0] A,
  output [5:0] out_or
);

  assign out_or = B | A;  // OR_Gate or_1, 6 bits wide
endmodule

module Shif_der (
  input  [5:0] A,
  output [5:0] Shift_der,
  output carr
);


  assign carr = A[0];
  assign Shift_der = {A[0], A[5:1]};
endmodule

module cir_shif_iz (
  input  [5:0] A,
  output Carr,
  output [5:0] Shif_iz
);


  assign Carr = A[5];
  assign Shif_iz = {A[4:0], A[5]};
endmodule

module Cir_Alu (
  input  [3:0] Menu,
  input  [5:0] A,
  input  [5:0] B,
  output [5:0] Resultado,
  output Carry,
  output Overflow,
  output Cero,
  output Negativo
);

  wire cir_shif_iz_1_carr, Cout, not_1_out, not_3_out, Over, res, shif_der_1_carr;
  wire [5:0] cir_and_1_out_and, cir_shif_iz_1_shif_iz, circ_add_1_s, circ_or_1_out_or, multiplexer_1_out,
       multiplexer_2_out, not_2_out, shif_der_1_shift_der;

  not not_1 (not_1_out, Menu[1]);
  and and_1 (res, not_1_out, Menu[0]);
  assign not_2_out = ~B;  // NOT_Gate not_2, 6 bits wide
  Shif_der shif_der_1 (.A(A), .Shift_der(shif_der_1_shift_der), .carr(shif_der_1_carr));
  cir_shif_iz cir_shif_iz_1 (.A(A), .Carr(cir_shif_iz_1_carr), .Shif_iz(cir_shif_iz_1_shif_iz));
  Multiplexer #(.width(6)) multiplexer_1 (.in0(B), .in1(not_2_out), .out(multiplexer_1_out), .sel(res));
  Multiplexer #(.select(2), .width(6)) multiplexer_2 (
    .in0(A), .in1(shif_der_1_shift_der), .in2(cir_shif_iz_1_shif_iz), .out(multiplexer_2_out), .sel(Menu[3:2]));  // open: in3
  not not_3 (not_3_out, res);
  and and_2 (Carry, Cout, not_3_out);
  and and_3 (Overflow, Over, res);
  Circ_add circ_add_1 (
    .res(res), .B(multiplexer_1_out), .A(multiplexer_2_out), .S(circ_add_1_s), .Over(Over), .cero(Cero),
    .negativo(Negativo), .Cout(Cout));
  Cir_and cir_and_1 (.B(B), .A(multiplexer_2_out), .out_and(cir_and_1_out_and));
  Circ_or circ_or_1 (.B(B), .A(multiplexer_2_out), .out_or(circ_or_1_out_or));
  Multiplexer #(.select(2), .width(6)) multiplexer_3 (
    .in0(circ_add_1_s), .in1(circ_add_1_s), .in2(cir_and_1_out_and), .in3(circ_or_1_out_or), .out(Resultado),
    .sel(Menu[1:0]));

  // Other names for the same wires on the sheet: op1[1:0] = Menu[1:0]; op2[1:0] = Menu[3:2]
endmodule

module Final (
  input  [3:0] Menu,
  input  [5:0] A,
  input  [5:0] B,
  output [5:0] out_4
);

  wire cir_alu_1_carry, cir_alu_1_cero, cir_alu_1_negativo, cir_alu_1_overflow;

  Cir_Alu cir_alu_1 (
    .Menu(Menu), .A(A), .B(B), .Resultado(out_4), .Carry(cir_alu_1_carry), .Overflow(cir_alu_1_overflow),
    .Cero(cir_alu_1_cero), .Negativo(cir_alu_1_negativo));
  LedBar #(.matrixcols(4)) ledbar_1 (
    .led0(cir_alu_1_overflow), .led1(cir_alu_1_cero), .led2(cir_alu_1_negativo), .led3(cir_alu_1_carry));

  // Notes on the sheet:
  //   00 SUMA
  //   01 RESTA
  //   10 AND
  //   11 OR
  //   1000 IZQUIERDA
  //   0100 DERECHA
endmodule
